// Logisim project 2.0 Artur CPU.circ as structural Verilog
module main (
  input  [1:0] Select_Address,
  input  [15:0] Immediate_num,
  input  [1:0] Select_Write,
  input  [15:0] Memory_Location,
  input  [2:0] Op_Code,
  input  Clear,
  input  [3:0] A,
  input  [3:0] B,
  input  [3:0] Register_num,
  output [15:0] ALU_Output,
  output [15:0] Register_A,
  output [15:0] Register_B
);

  wire Clock__Write_out;
  wire [15:0] multiplexer_1_out, multiplexer_2_out, ram_1_data;

  RAM #(.addrWidth(16), .dataWidth(16)) ram_1 (.addr(multiplexer_1_out), .data(ram_1_data));  // open: sel, clk, ld, clr
  Multiplexer #(.select(2), .width(16), .enable("false")) multiplexer_1 (
    .in1(Immediate_num), .in2(Register_A), .in3(Register_B), .out(multiplexer_1_out), .sel(Select_Address));  // open: in0
  Clock Clock__Write (.out(Clock__Write_out));
  Multiplexer #(.select(2), .width(16), .enable("false")) multiplexer_2 (
    .in0(Immediate_num), .in2(ram_1_data), .in3(ALU_Output), .out(multiplexer_2_out), .sel(Select_Write));  // open: in1
  Register_File Register_File (
    ._16_Bit_Input(multiplexer_2_out), .Clock__Write(Clock__Write_out), .Register_num(Register_num),
    .Clear__Erase(Clear), .Register_A(A), .Register_B(B), .A_Output(Register_A), .B_Output(Register_B));
  // ALU ALU: pin names not known; wires that end beside it: Register_A, Register_B, Op_Code, ALU_Output
endmodule

module ALU (
  input  [15:0] Input_1,
  input  [15:0] Input_2,
  input  Exe,
  input  Reset,
  input  [3:0] Op_Code,
  output [15:0] Resultant
);

  wire [15:0] demultiplexer_1_out0, demultiplexer_1_out1, demultiplexer_1_out2, demultiplexer_1_out3,
       demultiplexer_2_out0, demultiplexer_2_out1, demultiplexer_2_out2, demultiplexer_2_out3, divider_1_out,
       multiplexer_1_out, multiplier_1_out, subtractor_1_out, The_Artur_Adder__16_bit_result;

  Demultiplexer #(.select(3), .width(16)) demultiplexer_1 (
    .out0(demultiplexer_1_out0), .out1(demultiplexer_1_out1), .out2(demultiplexer_1_out2),
    .out3(demultiplexer_1_out3), .in(Input_1), .sel(Op_Code[2:0]));  // open: out4, out5, out6, out7, en
  Demultiplexer #(.select(3), .width(16)) demultiplexer_2 (
    .out0(demultiplexer_2_out0), .out1(demultiplexer_2_out1), .out2(demultiplexer_2_out2),
    .out3(demultiplexer_2_out3), .in(Input_2), .sel(Op_Code[2:0]));  // open: out4, out5, out6, out7, en
  The_Artur_Adder The_Artur_Adder (
    .Input_1(demultiplexer_1_out0), .Input_2(demultiplexer_2_out0),
    ._16_Bit_Result(The_Artur_Adder__16_bit_result));  // open: Carry_Out, _20_Bit_Result
  Subtractor #(.width(16)) subtractor_1 (
    .a(demultiplexer_1_out1), .b(demultiplexer_2_out1), .out(subtractor_1_out));  // open: bin, bout
  Multiplier #(.width(16)) multiplier_1 (
    .a(demultiplexer_1_out2), .b(demultiplexer_2_out2), .out(multiplier_1_out));  // open: cin, cout
  Divider #(.width(16)) divider_1 (
    .a(demultiplexer_1_out3), .b(demultiplexer_2_out3), .out(divider_1_out));  // open: upper, rem
  Multiplexer #(.select(3), .width(16)) multiplexer_1 (
    .in0(The_Artur_Adder__16_bit_result), .in1(subtractor_1_out), .in2(multiplier_1_out),
    .in3(divider_1_out), .out(multiplexer_1_out), .sel(Op_Code[2:0]));  // open: in4, in5, in6, in7, en
  Register #(.width(16)) register_1 (.D(multiplexer_1_out), .Q(Resultant), .clk(Exe), .clr(Reset));  // open: en
endmodule

module Register_File (
  input  [15:0] _16_Bit_Input,
  input  Clock__Write,
  input  [3:0] Register_A,
  input  [3:0] Register_num,
  input  [3:0] Register_B,
  input  Clear__Erase,
  output [15:0] A_Output,
  output [15:0] B_Output
);

  wire demultiplexer_1_out0, demultiplexer_1_out1, demultiplexer_1_out2, demultiplexer_1_out3,
       demultiplexer_1_out4, demultiplexer_1_out5, demultiplexer_1_out6, demultiplexer_1_out7,
       demultiplexer_1_out8, demultiplexer_1_out9, demultiplexer_1_out10, demultiplexer_1_out11,
       demultiplexer_1_out12, demultiplexer_1_out13, demultiplexer_1_out14, demultiplexer_1_out15;
  wire [15:0] the_vault_1_register_value, the_vault_2_register_value, the_vault_3_register_value,
       the_vault_4_register_value, the_vault_5_register_value, the_vault_6_register_value,
       the_vault_7_register_value, the_vault_8_register_value, the_vault_9_register_value,
       the_vault_10_register_value, the_vault_11_register_value, the_vault_12_register_value,
       the_vault_13_register_value, the_vault_14_register_value, the_vault_15_register_value,
       the_vault_16_register_value;

  Demultiplexer #(.select(4), .disabled(0), .enable("false")) demultiplexer_1 (
    .out0(demultiplexer_1_out0), .out1(demultiplexer_1_out1), .out2(demultiplexer_1_out2),
    .out3(demultiplexer_1_out3), .out4(demultiplexer_1_out4), .out5(demultiplexer_1_out5),
    .out6(demultiplexer_1_out6), .out7(demultiplexer_1_out7), .out8(demultiplexer_1_out8),
    .out9(demultiplexer_1_out9), .out10(demultiplexer_1_out10), .out11(demultiplexer_1_out11),
    .out12(demultiplexer_1_out12), .out13(demultiplexer_1_out13), .out14(demultiplexer_1_out14),
    .out15(demultiplexer_1_out15), .in(Clock__Write), .sel(Register_num));
  The_Vault the_vault_1 (
    ._16_Bit_Input(_16_Bit_Input), .Clock__Write(demultiplexer_1_out0), .Clear__Erase(Clear__Erase),
    .Register_Value(the_vault_1_register_value));
  The_Vault the_vault_2 (
    ._16_Bit_Input(_16_Bit_Input), .Clock__Write(demultiplexer_1_out1), .Clear__Erase(Clear__Erase),
    .Register_Value(the_vault_2_register_value));
  The_Vault the_vault_3 (
    ._16_Bit_Input(_16_Bit_Input), .Clock__Write(demultiplexer_1_out2), .Clear__Erase(Clear__Erase),
    .Register_Value(the_vault_3_register_value));
  The_Vault the_vault_4 (
    ._16_Bit_Input(_16_Bit_Input), .Clock__Write(demultiplexer_1_out3), .Clear__Erase(Clear__Erase),
    .Register_Value(the_vault_4_register_value));
  The_Vault the_vault_5 (
    ._16_Bit_Input(_16_Bit_Input), .Clock__Write(demultiplexer_1_out4), .Clear__Erase(Clear__Erase),
    .Register_Value(the_vault_5_register_value));
  The_Vault the_vault_6 (
    ._16_Bit_Input(_16_Bit_Input), .Clock__Write(demultiplexer_1_out5), .Clear__Erase(Clear__Erase),
    .Register_Value(the_vault_6_register_value));
  The_Vault the_vault_7 (
    ._16_Bit_Input(_16_Bit_Input), .Clock__Write(demultiplexer_1_out6), .Clear__Erase(Clear__Erase),
    .Register_Value(the_vault_7_register_value));
  The_Vault the_vault_8 (
    ._16_Bit_Input(_16_Bit_Input), .Clock__Write(demultiplexer_1_out7), .Clear__Erase(Clear__Erase),
    .Register_Value(the_vault_8_register_value));
  The_Vault the_vault_9 (
    ._16_Bit_Input(_16_Bit_Input), .Clock__Write(demultiplexer_1_out8), .Clear__Erase(Clear__Erase),
    .Register_Value(the_vault_9_register_value));
  The_Vault the_vault_10 (
    ._16_Bit_Input(_16_Bit_Input), .Clock__Write(demultiplexer_1_out9), .Clear__Erase(Clear__Erase),
    .Register_Value(the_vault_10_register_value));
  The_Vault the_vault_11 (
    ._16_Bit_Input(_16_Bit_Input), .Clock__Write(demultiplexer_1_out10), .Clear__Erase(Clear__Erase),
    .Register_Value(the_vault_11_register_value));
  The_Vault the_vault_12 (
    ._16_Bit_Input(_16_Bit_Input), .Clock__Write(demultiplexer_1_out11), .Clear__Erase(Clear__Erase),
    .Register_Value(the_vault_12_register_value));
  The_Vault the_vault_13 (
    ._16_Bit_Input(_16_Bit_Input), .Clock__Write(demultiplexer_1_out12), .Clear__Erase(Clear__Erase),
    .Register_Value(the_vault_13_register_value));
  The_Vault the_vault_14 (
    ._16_Bit_Input(_16_Bit_Input), .Clock__Write(demultiplexer_1_out13), .Clear__Erase(Clear__Erase),
    .Register_Value(the_vault_14_register_value));
  The_Vault the_vault_15 (
    ._16_Bit_Input(_16_Bit_Input), .Clock__Write(demultiplexer_1_out14), .Clear__Erase(Clear__Erase),
    .Register_Value(the_vault_15_register_value));
  The_Vault the_vault_16 (
    ._16_Bit_Input(_16_Bit_Input), .Clock__Write(demultiplexer_1_out15), .Clear__Erase(Clear__Erase),
    .Register_Value(the_vault_16_register_value));
  Multiplexer #(.select(4), .width(16)) multiplexer_1 (
    .in0(the_vault_1_register_value), .in1(the_vault_2_register_value), .in2(the_vault_3_register_value),
    .in3(the_vault_4_register_value), .in4(the_vault_5_register_value), .in5(the_vault_6_register_value),
    .in6(the_vault_7_register_value), .in7(the_vault_8_register_value), .in8(the_vault_9_register_value),
    .in9(the_vault_10_register_value), .in10(the_vault_11_register_value),
    .in11(the_vault_12_register_value), .in12(the_vault_13_register_value),
    .in13(the_vault_14_register_value), .in14(the_vault_15_register_value),
    .in15(the_vault_16_register_value), .out(A_Output), .sel(Register_A));  // open: en
  Multiplexer #(.select(4), .width(16)) multiplexer_2 (
    .in0(the_vault_1_register_value), .in1(the_vault_2_register_value), .in2(the_vault_3_register_value),
    .in3(the_vault_4_register_value), .in4(the_vault_5_register_value), .in5(the_vault_6_register_value),
    .in6(the_vault_7_register_value), .in7(the_vault_8_register_value), .in8(the_vault_9_register_value),
    .in9(the_vault_10_register_value), .in10(the_vault_11_register_value),
    .in11(the_vault_12_register_value), .in12(the_vault_13_register_value),
    .in13(the_vault_14_register_value), .in14(the_vault_15_register_value),
    .in15(the_vault_16_register_value), .out(B_Output), .sel(Register_B));  // open: en
endmodule

module The_Artur_Adder (
  input  [15:0] Input_1,
  input  [15:0] Input_2,
  output [15:0] _16_Bit_Result,
  output [19:0] _20_Bit_Result,
  output Carry_Out
);

  wire AND_2_out, AND_3_out, AND_4_out, AND_out, button_1_out, button_2_out, clock_1_out,
       full_adder_1_carry_out, full_adder_2_carry_out, full_adder_3_carry_out, full_adder_4_carry_out,
       full_adder_5_carry_out, full_adder_6_carry_out, full_adder_7_carry_out, full_adder_8_carry_out,
       full_adder_9_carry_out, full_adder_10_carry_out, full_adder_11_carry_out, full_adder_12_carry_out,
       full_adder_13_carry_out, OR_2_out, OR_out, XOR_2_out, XOR_out;

  xor XOR (XOR_out, Input_1[0], Input_2[0]);
  xor XOR_2 (XOR_2_out, Input_1[1], Input_2[1]);
  and AND (AND_out, Input_1[0], Input_2[0]);
  and AND_2 (AND_2_out, Input_1[1], Input_2[1]);
  xor XOR_3 (_16_Bit_Result[0], 1'b0, XOR_out);
  and AND_3 (AND_3_out, 1'b0, XOR_out);
  xor XOR_4 (_16_Bit_Result[1], OR_out, XOR_2_out);
  and AND_4 (AND_4_out, OR_out, XOR_2_out);
  Full_Adder full_adder_1 (
    .Bit_of_Number_1(Input_1[2]), .Bit_of_Number_2(Input_2[2]), .Carry_In(OR_2_out),
    .Carry_Out(full_adder_1_carry_out), .Sum(_16_Bit_Result[2]));
  Full_Adder full_adder_2 (
    .Bit_of_Number_1(Input_1[3]), .Bit_of_Number_2(Input_2[3]), .Carry_In(full_adder_1_carry_out),
    .Carry_Out(full_adder_2_carry_out), .Sum(_16_Bit_Result[3]));
  Full_Adder full_adder_3 (
    .Bit_of_Number_1(Input_1[4]), .Bit_of_Number_2(Input_2[4]), .Carry_In(full_adder_2_carry_out),
    .Carry_Out(full_adder_3_carry_out), .Sum(_16_Bit_Result[4]));
  Full_Adder full_adder_4 (
    .Bit_of_Number_1(Input_1[5]), .Bit_of_Number_2(Input_2[5]), .Carry_In(full_adder_3_carry_out),
    .Carry_Out(full_adder_4_carry_out), .Sum(_16_Bit_Result[5]));
  Full_Adder full_adder_5 (
    .Bit_of_Number_1(Input_1[6]), .Bit_of_Number_2(Input_2[6]), .Carry_In(full_adder_4_carry_out),
    .Carry_Out(full_adder_5_carry_out), .Sum(_16_Bit_Result[6]));
  Full_Adder full_adder_6 (
    .Bit_of_Number_1(Input_1[7]), .Bit_of_Number_2(Input_2[7]), .Carry_In(full_adder_5_carry_out),
    .Carry_Out(full_adder_6_carry_out), .Sum(_16_Bit_Result[7]));
  Full_Adder full_adder_7 (
    .Bit_of_Number_1(Input_1[8]), .Bit_of_Number_2(Input_2[8]), .Carry_In(full_adder_6_carry_out),
    .Carry_Out(full_adder_7_carry_out), .Sum(_16_Bit_Result[8]));
  Full_Adder full_adder_8 (
    .Bit_of_Number_1(Input_1[9]), .Bit_of_Number_2(Input_2[9]), .Carry_In(full_adder_7_carry_out),
    .Carry_Out(full_adder_8_carry_out), .Sum(_16_Bit_Result[9]));
  Full_Adder full_adder_9 (
    .Bit_of_Number_1(Input_1[10]), .Bit_of_Number_2(Input_2[10]), .Carry_In(full_adder_8_carry_out),
    .Carry_Out(full_adder_9_carry_out), .Sum(_16_Bit_Result[10]));
  Full_Adder full_adder_10 (
    .Bit_of_Number_1(Input_1[11]), .Bit_of_Number_2(Input_2[11]), .Carry_In(full_adder_9_carry_out),
    .Carry_Out(full_adder_10_carry_out), .Sum(_16_Bit_Result[11]));
  Full_Adder full_adder_11 (
    .Bit_of_Number_1(Input_1[12]), .Bit_of_Number_2(Input_2[12]), .Carry_In(full_adder_10_carry_out),
    .Carry_Out(full_adder_11_carry_out), .Sum(_16_Bit_Result[12]));
  Full_Adder full_adder_12 (
    .Bit_of_Number_1(Input_1[13]), .Bit_of_Number_2(Input_2[13]), .Carry_In(full_adder_11_carry_out),
    .Carry_Out(full_adder_12_carry_out), .Sum(_16_Bit_Result[13]));
  Full_Adder full_adder_13 (
    .Bit_of_Number_1(Input_1[14]), .Bit_of_Number_2(Input_2[14]), .Carry_In(full_adder_12_carry_out),
    .Carry_Out(full_adder_13_carry_out), .Sum(_16_Bit_Result[14]));
  Full_Adder full_adder_14 (
    .Bit_of_Number_1(Input_1[15]), .Bit_of_Number_2(Input_2[15]), .Carry_In(full_adder_13_carry_out),
    .Carry_Out(Carry_Out), .Sum(_16_Bit_Result[15]));
  Full_Adder full_adder_15 (
    .Bit_of_Number_1(1'b0), .Bit_of_Number_2(1'b0), .Carry_In(Carry_Out), .Sum(_20_Bit_Result[16]));  // open: Carry_Out
  or OR (OR_out, AND_3_out, AND_out);
  or OR_2 (OR_2_out, AND_4_out, AND_2_out);
  Hex_Digit_Display hex_digit_display_1 (.value({3'b000, _20_Bit_Result[16]}));  // open: dp
  Hex_Digit_Display hex_digit_display_2 (.value(_16_Bit_Result[11:8]));  // open: dp
  Hex_Digit_Display hex_digit_display_3 (.value(_16_Bit_Result[15:12]));  // open: dp
  Clock clock_1 (.out(clock_1_out));
  Hex_Digit_Display hex_digit_display_4 (.value(_16_Bit_Result[7:4]));  // open: dp
  Hex_Digit_Display hex_digit_display_5 (.value(_16_Bit_Result[3:0]));  // open: dp
  TTY tty_1 (.data(_16_Bit_Result[6:0]), .clk(clock_1_out), .we(button_2_out), .clr(button_1_out));
  Button button_1 (.out(button_1_out));
  Button button_2 (.out(button_2_out));

  assign {_20_Bit_Result[19:17], _20_Bit_Result[15:0]} = {3'b000, _16_Bit_Result};

  // Notes on the sheet:
  //   Sum
  //   Carry Out
  //   The Carry Out is to keep it modular
  //   Don't let this fool you, there are 16 modules + 1 extra for a resultant value that is greater than 16 bit.
endmodule

module Full_Adder (
  input  Carry_In,
  input  Bit_of_Number_1,
  input  Bit_of_Number_2,
  output Sum,
  output Carry_Out
);

  wire AND_2_out, AND_out, XOR_out;

  xor XOR (XOR_out, Bit_of_Number_1, Bit_of_Number_2);
  and AND (AND_out, Bit_of_Number_1, Bit_of_Number_2);
  xor XOR_2 (Sum, Carry_In, XOR_out);
  and AND_2 (AND_2_out, Carry_In, XOR_out);
  or OR (Carry_Out, AND_2_out, AND_out);
endmodule

module Young_D__Flipper (
  input  Q,
  input  Clk,
  input  Reset,
  output Q_2
);

  wire nand_1_out, nand_2_out, nand_4_out, not_1_out;

  not not_1 (not_1_out, Q);
  nand nand_1 (nand_1_out, Q, Clk);
  nand nand_2 (nand_2_out, not_1_out, Clk);
  nand nand_3 (Q_2, nand_1_out, nand_4_out);
  nand nand_4 (nand_4_out, Q_2, ~Reset, nand_2_out);  // NAND_Gate
endmodule

module The_Vault (
  input  [15:0] _16_Bit_Input,
  input  Clock__Write,
  input  Clear__Erase,
  output [15:0] Register_Value
);

  Young_D__Flipper young_d_flipper_1 (
    .Q(_16_Bit_Input[0]), .Clk(Clock__Write), .Reset(Clear__Erase), .Q_2(Register_Value[0]));
  Young_D__Flipper young_d_flipper_2 (
    .Q(_16_Bit_Input[1]), .Clk(Clock__Write), .Reset(Clear__Erase), .Q_2(Register_Value[1]));
  Young_D__Flipper young_d_flipper_3 (
    .Q(_16_Bit_Input[2]), .Clk(Clock__Write), .Reset(Clear__Erase), .Q_2(Register_Value[2]));
  Young_D__Flipper young_d_flipper_4 (
    .Q(_16_Bit_Input[3]), .Clk(Clock__Write), .Reset(Clear__Erase), .Q_2(Register_Value[3]));
  Young_D__Flipper young_d_flipper_5 (
    .Q(_16_Bit_Input[4]), .Clk(Clock__Write), .Reset(Clear__Erase), .Q_2(Register_Value[4]));
  Young_D__Flipper young_d_flipper_6 (
    .Q(_16_Bit_Input[5]), .Clk(Clock__Write), .Reset(Clear__Erase), .Q_2(Register_Value[5]));
  Young_D__Flipper young_d_flipper_7 (
    .Q(_16_Bit_Input[6]), .Clk(Clock__Write), .Reset(Clear__Erase), .Q_2(Register_Value[6]));
  Young_D__Flipper young_d_flipper_8 (
    .Q(_16_Bit_Input[7]), .Clk(Clock__Write), .Reset(Clear__Erase), .Q_2(Register_Value[7]));
  Young_D__Flipper young_d_flipper_9 (
    .Q(_16_Bit_Input[8]), .Clk(Clock__Write), .Reset(Clear__Erase), .Q_2(Register_Value[8]));
  Young_D__Flipper young_d_flipper_10 (
    .Q(_16_Bit_Input[9]), .Clk(Clock__Write), .Reset(Clear__Erase), .Q_2(Register_Value[9]));
  Young_D__Flipper young_d_flipper_11 (
    .Q(_16_Bit_Input[10]), .Clk(Clock__Write), .Reset(Clear__Erase), .Q_2(Register_Value[10]));
  Young_D__Flipper young_d_flipper_12 (
    .Q(_16_Bit_Input[11]), .Clk(Clock__Write), .Reset(Clear__Erase), .Q_2(Register_Value[11]));
  Young_D__Flipper young_d_flipper_13 (
    .Q(_16_Bit_Input[12]), .Clk(Clock__Write), .Reset(Clear__Erase), .Q_2(Register_Value[12]));
  Young_D__Flipper young_d_flipper_14 (
    .Q(_16_Bit_Input[13]), .Clk(Clock__Write), .Reset(Clear__Erase), .Q_2(Register_Value[13]));
  Young_D__Flipper young_d_flipper_15 (
    .Q(_16_Bit_Input[14]), .Clk(Clock__Write), .Reset(Clear__Erase), .Q_2(Register_Value[14]));
  Young_D__Flipper young_d_flipper_16 (
    .Q(_16_Bit_Input[15]), .Clk(Clock__Write), .Reset(Clear__Erase), .Q_2(Register_Value[15]));

  // Notes on the sheet:
  //   <--- Bug
endmodule

module Decafer (
  input  [15:0] Instruction_from_ROM,
  output [3:0] Opcode,
  output [7:0] Immediate_num,
  output [3:0] Operand_1__Usually_the_destination_register,
  output [3:0] Operand_2,
  output [3:0] Operand_3
);

  Demultiplexer #(.select(4), .width(12), .tristate("true"), .enable("false")) demultiplexer_1 (
    .out0({Immediate_num, Operand_1__Usually_the_destination_register}),
    .out1({Operand_3, Operand_2, Operand_1__Usually_the_destination_register}),
    .in(Instruction_from_ROM[15:4]), .sel(Instruction_from_ROM[3:0]));  // open: out2, out3, out4, out5, out6, out7, out8, out9, out10, out11, out12, out13, out14, out15

  assign Opcode = Instruction_from_ROM[3:0];
endmodule

module GrandFather_Clock (
);

  T_Flip_Flop t_ff_1 ();  // open: clk, T, Q, Qn, preset, reset, en
endmodule

module Full_Adder_Twos (
  input  Carry_In,
  input  Bit_of_Number_1,
  input  Bit_of_Number_2,
  output Sum,
  output Carry_Out
);

  wire and_1_out, and_2_out, AND_3_out, or_1_out, XOR_out;

  xor XOR (XOR_out, Bit_of_Number_1, Bit_of_Number_2);
  and and_1 (and_1_out, Carry_In, Bit_of_Number_1);
  and and_2 (and_2_out, Carry_In, Bit_of_Number_2);
  and AND_3 (AND_3_out, Bit_of_Number_1, Bit_of_Number_2);
  xor XOR_2 (Sum, Carry_In, XOR_out);
  or or_1 (or_1_out, and_1_out, and_2_out);
  or OR_2 (Carry_Out, or_1_out, AND_3_out);
endmodule

module Yound_D__Flipper_Old (
  input  Data_Bit,
  input  Clock,
  input  Clear,
  output out_4,
  output out_5
);

  wire nand_1_out, nand_2_out, nand_3_out, or_1_out;

  nand nand_1 (nand_1_out, Data_Bit, Data_Bit);
  nand nand_2 (nand_2_out, Data_Bit, Clock);
  or or_1 (or_1_out, Clear, out_5);
  nand nand_3 (nand_3_out, Clock, nand_1_out);
  nand nand_4 (out_4, nand_2_out, or_1_out);
  nand nand_5 (out_5, out_4, nand_3_out);
endmodule
