// Logisim project CompArch-FinalProject-2015-CPU.circ as structural Verilog
module Artur_s_Room (
);

  wire button_1_out, fetch_module_1_p2, fetch_module_1_p6, fetch_module_1_p7, fetch_module_1_p8,
       fetch_module_1_p9, fetch_module_1_p10, fetch_module_1_p11, pc_controller_1_p15, pc_controller_1_p18,
       pc_controller_1_p19, register_file_1_p1, register_file_1_p2, register_file_1_p3, register_file_1_p5,
       register_file_1_p6, register_file_1_p7, register_file_1_p8, smart_clock_1_clk, state_keeper_1_s2,
       state_keeper_1_s3, toggle_circut_1_out;
  wire [11:0] fetch_module_1_p5, multiplexer_1_out;
  wire [15:0] fetch_module_1_p3;

  // FETCH_MODULE fetch_module_1: pin names not known; wires that end beside it: 1'b0, fetch_module_1_p2, fetch_module_1_p3, 1'b0, fetch_module_1_p5, fetch_module_1_p6, fetch_module_1_p7, fetch_module_1_p8, fetch_module_1_p9, fetch_module_1_p10, fetch_module_1_p11
  not not_1 (fetch_module_1_p2, toggle_circut_1_out);
  State_Keeper state_keeper_1 (
    .Keep(1'b0), .S1(fetch_module_1_p6), .S2(state_keeper_1_s2), .S3(state_keeper_1_s3),
    .Reset(fetch_module_1_p2), .Clk(smart_clock_1_clk));
  SMART_CLOCK smart_clock_1 (.Clk(smart_clock_1_clk), .ON(toggle_circut_1_out));
  Toggle_Circut toggle_circut_1 (.Input(button_1_out), .Out(toggle_circut_1_out));
  Button button_1 (.out(button_1_out));
  // Register_File register_file_1: pin names not known; wires that end beside it: register_file_1_p1, register_file_1_p2, register_file_1_p3, fetch_module_1_p2, register_file_1_p5, register_file_1_p6, register_file_1_p7, register_file_1_p8
  // PC_Controller pc_controller_1: pin names not known; wires that end beside it: register_file_1_p2, fetch_module_1_p7, register_file_1_p3, fetch_module_1_p8, register_file_1_p5, fetch_module_1_p9, register_file_1_p6, fetch_module_1_p10, register_file_1_p1, fetch_module_1_p11, register_file_1_p7, state_keeper_1_s2, register_file_1_p8, state_keeper_1_s3, pc_controller_1_p15, pc_controller_1_p15, pc_controller_1_p15, pc_controller_1_p18, pc_controller_1_p19
  // ALU alu_1: pin names not known; wires that end beside it: pc_controller_1_p15, pc_controller_1_p15, pc_controller_1_p15, pc_controller_1_p19, pc_controller_1_p18
  Multiplexer #(.width(12), .enable("false")) multiplexer_1 (
    .in1(fetch_module_1_p5), .out(multiplexer_1_out), .sel(fetch_module_1_p6));  // open: in0
  RAM #(.addrWidth(12), .dataWidth(16), .bus("separate")) ram_1 (
    .addr(multiplexer_1_out), .data(fetch_module_1_p3));  // open: din, str, sel, clk, ld, clr
endmodule

module Nathan_s_Room (
);

  Button button_1 ();  // open: out
endmodule

module Nathans_Room_Copy (
);

  wire addressbus_1_next, addressbus_1_prepare, and_1_out, button_1_out, comparison_register_1_eq,
       comparison_register_1_gt, comparison_register_1_gte, comparison_register_1_lt,
       comparison_register_1_lte, fetch_module_1_end, ip_controller_1_set, not_1_out, not_2_out, or_1_out,
       or_2_out, or_3_out, or_4_out, pc_controller_2_0_1_alu_exe, pc_controller_2_0_1_compare,
       pc_controller_2_0_1_get_next_value, pc_controller_2_0_1_next_opcode, pc_controller_2_0_1_pc_exe,
       pc_controller_2_0_1_ram_clk, pc_controller_2_0_1_ram_exe, pc_controller_2_0_1_read_write,
       pc_controller_2_0_1_write, smart_clock_1_clk, state_keeper_1_s1, state_keeper_1_s2, state_keeper_1_s3,
       toggle_circut_1_out;
  wire [2:0] pc_controller_2_0_1_pc_op;
  wire [3:0] fetch_module_1_op1, fetch_module_1_op2, fetch_module_1_op3, fetch_module_1_op_code,
       pc_controller_2_0_1_alu_operation, pc_controller_2_0_1_reg_destination, pc_controller_2_0_1_reg_src_a,
       pc_controller_2_0_1_reg_src_b;
  wire [11:0] addressbus_1_ram_address, fetch_module_1_select, multiplexer_1_out,
       pc_controller_2_0_1_ip_set_to, pc_controller_2_0_1_ram_address;
  wire [15:0] addressbus_1_ram_write_value, addressbus_1_readvalue, alu_1_resultant, controlled_buffer_1_out,
       controlled_buffer_2_out, fetch_module_1_imm, pc_controller_2_0_1_alu_param_1,
       pc_controller_2_0_1_alu_parameter_2, pc_controller_2_0_1_compare_a, pc_controller_2_0_1_compare_b,
       pc_controller_2_0_1_ram_write_value, pc_controller_2_0_1_reg_destination_value,
       register_filer_1_val_a, register_filer_1_val_b;

  Comparison_Register comparison_register_1 (
    .A(pc_controller_2_0_1_compare_a), .B(pc_controller_2_0_1_compare_b),
    .Compare(pc_controller_2_0_1_compare), .RST(not_1_out), .GT(comparison_register_1_gt),
    .EQ(comparison_register_1_eq), .LT(comparison_register_1_lt), .LTE(comparison_register_1_lte),
    .GTE(comparison_register_1_gte));
  IP_Controller ip_controller_1 (
    .OP(pc_controller_2_0_1_pc_op), .GT(comparison_register_1_gt), .EQ(comparison_register_1_eq),
    .LT(comparison_register_1_lt), .LTE(comparison_register_1_lte), .GTE(comparison_register_1_gte),
    .Clk(pc_controller_2_0_1_pc_exe), .SET(ip_controller_1_set));
  not not_1 (not_1_out, toggle_circut_1_out);
  Button button_1 (.out(button_1_out));
  Toggle_Circut toggle_circut_1 (.Input(button_1_out), .Out(toggle_circut_1_out));
  State_Keeper state_keeper_1 (
    .Keep(not_1_out), .S1(state_keeper_1_s1), .S2(state_keeper_1_s2), .S3(state_keeper_1_s3),
    .Reset(or_1_out), .Clk(and_1_out));
  and and_1 (and_1_out, smart_clock_1_clk, ~fetch_module_1_end);  // AND_Gate
  SMART_CLOCK smart_clock_1 (.Clk(smart_clock_1_clk), .ON(toggle_circut_1_out));
  Register_Filer register_filer_1 (
    .Dest(pc_controller_2_0_1_reg_destination), .Clk(pc_controller_2_0_1_write),
    .Val(pc_controller_2_0_1_reg_destination_value), .RST(not_1_out), .Src_A(pc_controller_2_0_1_reg_src_a),
    .Src_B(pc_controller_2_0_1_reg_src_b), .Val_A(register_filer_1_val_a), .Val_B(register_filer_1_val_b));
  FETCH_MODULE fetch_module_1 (
    .IPTO(pc_controller_2_0_1_ip_set_to), .SETIP(ip_controller_1_set), .RST(not_1_out),
    .GETNEXT(pc_controller_2_0_1_get_next_value), .RECIEVE(controlled_buffer_2_out),
    .SELECT(fetch_module_1_select), .Clk(state_keeper_1_s1), .END(fetch_module_1_end),
    .S3(state_keeper_1_s1), .OP_CODE(fetch_module_1_op_code), .OP1(fetch_module_1_op1),
    .OP2(fetch_module_1_op2), .OP3(fetch_module_1_op3), .IMM(fetch_module_1_imm));
  or or_1 (or_1_out, not_1_out, pc_controller_2_0_1_next_opcode);
  PC_Controller_2_0 pc_controller_2_0_1 (
    .Compare_A(pc_controller_2_0_1_compare_a), .Compare_B(pc_controller_2_0_1_compare_b),
    .Compare(pc_controller_2_0_1_compare), .PC_Op(pc_controller_2_0_1_pc_op),
    .PC_Exe(pc_controller_2_0_1_pc_exe), .IP_Set_To(pc_controller_2_0_1_ip_set_to),
    .Write(pc_controller_2_0_1_write), .Reg_Destination(pc_controller_2_0_1_reg_destination),
    .Reg_Destination_Value(pc_controller_2_0_1_reg_destination_value),
    .Reg_Src_A(pc_controller_2_0_1_reg_src_a), .Reg_Src_B(pc_controller_2_0_1_reg_src_b),
    .Reg_Value_A(register_filer_1_val_a), .Reg_Value_B(register_filer_1_val_b),
    .Next_Opcode(pc_controller_2_0_1_next_opcode), .OP(fetch_module_1_op_code), .OPER1(fetch_module_1_op1),
    .OPER2(fetch_module_1_op2), .OPER3(fetch_module_1_op3), .IMM(fetch_module_1_imm), .S2(state_keeper_1_s2),
    .S3(state_keeper_1_s3), .Get_Next_Value(pc_controller_2_0_1_get_next_value),
    .ALU_Operation(pc_controller_2_0_1_alu_operation), .ALU_Param_1(pc_controller_2_0_1_alu_param_1),
    .ALU_Parameter_2(pc_controller_2_0_1_alu_parameter_2), .ALU_Result(alu_1_resultant),
    .ALU_Exe(pc_controller_2_0_1_alu_exe), .RAM_Address(pc_controller_2_0_1_ram_address),
    .RAM_Write_Value(pc_controller_2_0_1_ram_write_value), .RAM_Read_Value(addressbus_1_readvalue),
    .Read_Write(pc_controller_2_0_1_read_write), .RAM_Clk(pc_controller_2_0_1_ram_clk),
    .RAM_Exe(pc_controller_2_0_1_ram_exe));
  ALU alu_1 (
    .Input_1(pc_controller_2_0_1_alu_param_1), .Input_2(pc_controller_2_0_1_alu_parameter_2),
    .Op_Code(pc_controller_2_0_1_alu_operation), .Exe(pc_controller_2_0_1_alu_exe),
    .Reset(state_keeper_1_s1), .Resultant(alu_1_resultant));
  or or_2 (or_2_out, pc_controller_2_0_1_get_next_value, state_keeper_1_s1);
  AddressBus addressbus_1 (
    .Address(pc_controller_2_0_1_ram_address), .WriteValue(pc_controller_2_0_1_ram_write_value),
    .ReadValue(addressbus_1_readvalue), .RW(pc_controller_2_0_1_read_write),
    .Clk(pc_controller_2_0_1_ram_clk), .Exe(pc_controller_2_0_1_ram_exe), .S1(state_keeper_1_s1),
    .Prepare(addressbus_1_prepare), .NEXT(addressbus_1_next), .RAM_Address(addressbus_1_ram_address),
    .RAM_Write_Value(addressbus_1_ram_write_value), .RAM_Read_Value(controlled_buffer_2_out));
  Multiplexer #(.width(12), .disabled(0), .enable("false")) multiplexer_1 (
    .in0(addressbus_1_ram_address), .in1(fetch_module_1_select), .out(multiplexer_1_out), .sel(or_2_out));
  or or_3 (or_3_out, or_2_out, ~addressbus_1_prepare);  // OR_Gate
  or or_4 (or_4_out, or_2_out, ~addressbus_1_prepare);  // OR_Gate
  not not_2 (not_2_out, or_3_out);
  assign controlled_buffer_1_out = not_2_out ? addressbus_1_ram_write_value : 16'bz;  // Controlled_Buffer controlled_buffer_1
  RAM #(.addrWidth(12), .dataWidth(16)) ram_1 (
    .addr(multiplexer_1_out), .data(controlled_buffer_1_out), .clk(addressbus_1_next), .ld(or_4_out));  // open: sel, clr
  assign controlled_buffer_2_out = or_3_out ? controlled_buffer_1_out : 16'bz;  // Controlled_Buffer controlled_buffer_2
endmodule
