// Logisim project CompArch-FinalProject-2015-Library-Nathan.circ as structural Verilog: 17 circuits, main circuit main
module main (
  input  Enable,
  input  [15:0] NEXT,
  input  [15:0] NEXT_2,
  input  [15:0] Val,
  input  [11:0] Address,
  input  [15:0] Val_2,
  input  [11:0] Address_2,
  output [15:0] NEXT_3,
  output [15:0] NEXT_4,
  output [15:0] READ,
  output [15:0] READ_2
);

  wire addressbus_1_p6, addressbus_2_p6, addressbus_2_p8, addressbus_2_p9, clock_1_out, clock_2_out,
       clock_3_out, clock_4_out, clock_5_out, clock_6_out, not_1_out, not_2_out, not_3_out, not_4_out;
  wire [11:0] addressbus_1_p7, addressbus_2_p7;
  wire [15:0] addressbus_1_p8, addressbus_1_p9, controlled_buffer_5_out, controlled_buffer_6_out, ram_1_data,
       test_2_p1;

  assign NEXT_3 = Enable ? NEXT : 16'bz;  // Controlled_Buffer controlled_buffer_1
  Test test_1 (.A_Out(NEXT_3), .A_In(NEXT_3), .Direction(Enable), .B_In(NEXT_4), .B_Out(NEXT_4));
  not not_1 (not_1_out, Enable);
  Clock clock_1 (.out(clock_1_out));
  Clock clock_2 (.out(clock_2_out));
  assign NEXT_4 = not_1_out ? NEXT_2 : 16'bz;  // Controlled_Buffer controlled_buffer_2
  // AddressBus addressbus_1: pin names not known; wires that end beside it: Address_2, Val_2, READ_2, clock_1_out, clock_2_out, addressbus_1_p6, addressbus_1_p7, addressbus_1_p8, addressbus_1_p9
  Clock clock_3 (.out(clock_3_out));
  Clock clock_4 (.out(clock_4_out));
  // AddressBus addressbus_2: pin names not known; wires that end beside it: Address, Val, READ, clock_3_out, clock_4_out, addressbus_2_p6, addressbus_2_p7, addressbus_2_p8, addressbus_2_p9
  RAM #(.addrWidth(12), .dataWidth(16)) ram_1 (
    .addr(addressbus_1_p7), .data(ram_1_data), .clk(addressbus_1_p6), .ld(not_2_out));  // open: sel, clr
  not not_2 (not_2_out, clock_1_out);
  assign ram_1_data = addressbus_1_p6 ? addressbus_1_p8 : 16'bz;  // Controlled_Buffer controlled_buffer_3
  assign addressbus_1_p9 = not_3_out ? ram_1_data : 16'bz;  // Controlled_Buffer controlled_buffer_4
  not not_3 (not_3_out, addressbus_1_p6);
  Clock clock_5 (.out(clock_5_out));
  Clock clock_6 (.out(clock_6_out));
  assign controlled_buffer_5_out = addressbus_2_p6 ? test_2_p1 : 16'bz;  // Controlled_Buffer controlled_buffer_5
  RAM #(.addrWidth(12), .dataWidth(16)) ram_2 (
    .addr(addressbus_2_p7), .data(controlled_buffer_5_out), .clk(clock_5_out));  // open: sel, ld, clr
  assign controlled_buffer_6_out = not_4_out ? controlled_buffer_5_out : 16'bz;  // Controlled_Buffer controlled_buffer_6
  not not_4 (not_4_out, addressbus_2_p6);
  // Test test_2: pin names not known; wires that end beside it: test_2_p1, controlled_buffer_6_out, addressbus_2_p6, addressbus_2_p8, addressbus_2_p9
endmodule

// IP
module IP_Register (
  input  Set,
  input  [11:0] SetAddr,
  input  RST,
  input  Clk,
  output [11:0] Value,
  output EOF
);

  wire and_1_out, or_1_out;
  wire [11:0] adder_1_out, multiplexer_1_out;

  Register #(.width(12), .trigger("falling")) register_1 (
    .D(multiplexer_1_out), .Q(Value), .clk(or_1_out), .clr(RST));  // open: en
  Multiplexer #(.width(12), .enable("false")) multiplexer_1 (
    .in0(adder_1_out), .in1(SetAddr), .out(multiplexer_1_out), .sel(Set));
  or or_1 (or_1_out, Set, and_1_out);
  and and_1 (and_1_out, Clk, ~EOF);  // AND_Gate
  Adder #(.width(12)) adder_1 (.a(Value), .b(12'h1), .out(adder_1_out), .cout(EOF));  // open: cin
endmodule

// FCH
module Fetcher (
  input  [15:0] INST,
  input  Clk,
  input  [11:0] IP,
  input  RST,
  output [15:0] INST_2,
  output [11:0] GET
);

  Register #(.width(16), .trigger("falling")) BUFF (.D(INST), .Q(INST_2), .clk(Clk), .clr(RST));  // open: en

  assign GET = IP;
endmodule

// STAT
module State_Keeper (
  input  Keep,
  input  Reset,
  input  Clk,
  output S1,
  output S2,
  output S3
);

  wire adder_1_cout, or_1_out;
  wire [1:0] adder_1_out, multiplexer_1_out, register_1_q;

  Multiplexer #(.width(2), .enable("false")) multiplexer_1 (
    .in0(adder_1_out), .in1(register_1_q), .out(multiplexer_1_out), .sel(Keep));
  or or_1 (or_1_out, Reset, adder_1_cout);
  Demultiplexer #(.select(2), .enable("false")) demultiplexer_1 (
    .out0(S1), .out1(S2), .out2(S3), .in(Clk), .sel(register_1_q));  // open: out3
  Register #(.width(2), .trigger("falling")) register_1 (
    .D(multiplexer_1_out), .Q(register_1_q), .clk(Clk), .clr(or_1_out));  // open: en
  Adder #(.width(2)) adder_1 (.a(register_1_q), .b(2'b01), .out(adder_1_out), .cout(adder_1_cout));  // open: cin
endmodule

module Decoder (
  input  [15:0] INS_IN,
  output [3:0] OP_CODE,
  output [3:0] OPERAND1,
  output [3:0] OPERAND2,
  output [3:0] OPERAND3,
  output [15:0] Immediate
);

  wire [7:0] demultiplexer_1_out4;
  wire [11:0] demultiplexer_1_out6;

  Demultiplexer #(.select(4), .width(12), .tristate("true"), .disabled(0), .enable("false")) demultiplexer_1 (
    .out0({OPERAND1, OPERAND2, OPERAND3}), .out1({OPERAND1, OPERAND2, OPERAND3}),
    .out2({OPERAND1, OPERAND2, OPERAND3}), .out3({OPERAND1, OPERAND2, OPERAND3}),
    .out4({OPERAND1, demultiplexer_1_out4}), .out5({OPERAND1, OPERAND2, OPERAND3}),
    .out6(demultiplexer_1_out6), .out7(demultiplexer_1_out6), .out8(demultiplexer_1_out6),
    .out9(demultiplexer_1_out6), .out10(demultiplexer_1_out6), .out11(demultiplexer_1_out6),
    .out12({OPERAND1, OPERAND2, OPERAND3}), .out13({OPERAND1, OPERAND2, OPERAND3}),
    .out14({OPERAND1, OPERAND2, OPERAND3}), .in(INS_IN[11:0]), .sel(INS_IN[15:12]));  // open: out15
  assign Immediate = {{8{demultiplexer_1_out4[7]}}, demultiplexer_1_out4};  // Bit_Extender bit_extender_1
  assign Immediate = {{4{demultiplexer_1_out6[11]}}, demultiplexer_1_out6};  // Bit_Extender bit_extender_2

  assign OP_CODE = INS_IN[15:12];
endmodule

module Rdy (
  input  RDY,
  input  DNE,
  output OK
);

  wire and_1_out, and_2_out, not_1_out, or_1_out;

  and and_1 (and_1_out, RDY, ~OK);  // AND_Gate
  or or_1 (or_1_out, and_1_out, and_2_out);
  and and_2 (and_2_out, DNE, OK);
  not not_1 (not_1_out, OK);
  D_Flip_Flop d_ff_1 (.clk(or_1_out), .D(not_1_out), .Q(OK));  // open: Qn, preset, en, reset
endmodule

module Toggle_Circut (
  input  Input,
  output Out
);

  wire not_1_out;

  not not_1 (not_1_out, Out);
  D_Flip_Flop #(.trigger("falling")) d_ff_1 (.clk(Input), .D(not_1_out), .Q(Out));  // open: Qn, preset, en, reset
endmodule

// FCHMOD
module FETCH_MODULE (
  input  GETNEXT,
  input  [11:0] IPTO,
  input  SETIP,
  input  RST,
  input  [15:0] RECIEVE,
  input  Clk,
  input  S3,
  output [3:0] OP_CODE,
  output [3:0] OP1,
  output [3:0] OP2,
  output [3:0] OP3,
  output [15:0] IMM,
  output [11:0] SELECT,
  output END
);

  wire or_1_out, or_2_out;
  wire [11:0] ip_register_1_value;
  wire [15:0] decoder_1_immediate, fetcher_1_inst_2, register_1_q;

  Fetcher fetcher_1 (
    .INST(RECIEVE), .IP(ip_register_1_value), .RST(RST), .Clk(Clk), .GET(SELECT), .INST_2(fetcher_1_inst_2));
  Decoder decoder_1 (
    .INS_IN(fetcher_1_inst_2), .OP_CODE(OP_CODE), .OPERAND1(OP1), .OPERAND2(OP2), .OPERAND3(OP3),
    .Immediate(decoder_1_immediate));
  IP_Register ip_register_1 (
    .Set(SETIP), .SetAddr(IPTO), .RST(RST), .Clk(or_1_out), .EOF(END), .Value(ip_register_1_value));
  or or_1 (or_1_out, GETNEXT, Clk);
  Register #(.width(16), .trigger("falling")) register_1 (
    .D(RECIEVE), .Q(register_1_q), .clk(GETNEXT), .clr(or_2_out));  // open: en
  or or_2 (or_2_out, RST, S3);
  assign IMM = decoder_1_immediate | register_1_q;  // OR_Gate or_3, 16 bits wide
endmodule

// CLK
module SMART_CLOCK (
  input  ON,
  output Clk
);

  wire clock_1_out;

  and and_1 (Clk, ON, clock_1_out);
  Clock clock_1 (.out(clock_1_out));
endmodule

module PC_Controller (
  input  [15:0] RF_VALA,
  input  [15:0] RF_VALB,
  input  [15:0] ALUV,
  input  [11:0] RAMWADDR,
  input  [15:0] RAMWVAL,
  input  S2,
  input  S3,
  input  [15:0] IMM,
  input  [3:0] OP,
  input  [3:0] OPER1,
  input  [3:0] OPER2,
  input  [3:0] OPER3,
  output RF_CLK,
  output [3:0] RF_DEST,
  output [3:0] RF_SRCA,
  output [3:0] RF_SRCB,
  output [15:0] RF_DESTVAL,
  output [3:0] ALUOP,
  output [15:0] CMP_A,
  output [15:0] ALUP1,
  output [15:0] CMP_B,
  output [15:0] ALUP2,
  output CMP,
  output [2:0] IPCONTOP,
  output EXE,
  output IPCONTCLK,
  output [11:0] SETIPVAL,
  output EXE_2,
  output NEXT
);

  wire demultiplexer_2_out4, demultiplexer_5_out0, demultiplexer_5_out1, demultiplexer_5_out2,
       demultiplexer_5_out3, demultiplexer_5_out6, demultiplexer_5_out7, demultiplexer_5_out8,
       demultiplexer_5_out9, demultiplexer_5_out10, demultiplexer_5_out11;

  Subtractor #(.width(3)) subtractor_1 (.a(OP[2:0]), .b(3'b110), .out(IPCONTOP));  // open: bin, bout
  Demultiplexer #(.select(4), .width(4), .tristate("true"), .disabled(0), .enable("false")) demultiplexer_1 (
    .out0(RF_DEST), .out1(RF_DEST), .out2(RF_DEST), .out3(RF_DEST), .out4(RF_DEST), .out5(RF_SRCA),
    .out12(RF_SRCA), .in(OPER1), .sel(OP));  // open: out6, out7, out8, out9, out10, out11, out13, out14, out15
  Multiplexer #(.select(4), .width(16), .disabled(0), .enable("false")) multiplexer_1 (
    .in0(ALUV), .in1(ALUV), .in2(ALUV), .in3(ALUV), .in4(IMM), .out(RF_DESTVAL), .sel(OP));  // open: in5, in6, in7, in8, in9, in10, in11, in12, in13, in14, in15
  Demultiplexer #(.select(4), .disabled(0), .enable("false")) demultiplexer_2 (
    .out4(demultiplexer_2_out4), .in(S3), .sel(OP));  // open: out0, out1, out2, out3, out5, out6, out7, out8, out9, out10, out11, out12, out13, out14, out15
  Demultiplexer #(.select(4), .width(4), .tristate("true"), .disabled(0), .enable("false")) demultiplexer_3 (
    .out0(RF_SRCA), .out1(RF_SRCA), .out2(RF_SRCA), .out3(RF_SRCA), .out5(RF_SRCB), .in(OPER2), .sel(OP));  // open: out4, out6, out7, out8, out9, out10, out11, out12, out13, out14, out15
  or or_1 (EXE, demultiplexer_2_out4, demultiplexer_5_out0, demultiplexer_5_out3, demultiplexer_5_out1, demultiplexer_5_out2);
  Demultiplexer #(.select(4), .width(4), .tristate("true"), .disabled(0), .enable("false")) demultiplexer_4 (
    .out0(RF_SRCB), .out1(RF_SRCB), .out2(RF_SRCB), .out3(RF_SRCB), .in(OPER3), .sel(OP));  // open: out4, out5, out6, out7, out8, out9, out10, out11, out12, out13, out14, out15
  or or_2 (IPCONTCLK, demultiplexer_5_out6, demultiplexer_5_out7, demultiplexer_5_out8, demultiplexer_5_out9, demultiplexer_5_out10, demultiplexer_5_out11);
  Demultiplexer #(.select(4), .disabled(0), .enable("false")) demultiplexer_5 (
    .out0(demultiplexer_5_out0), .out1(demultiplexer_5_out1), .out2(demultiplexer_5_out2),
    .out3(demultiplexer_5_out3), .out4(NEXT), .out5(CMP), .out6(demultiplexer_5_out6),
    .out7(demultiplexer_5_out7), .out8(demultiplexer_5_out8), .out9(demultiplexer_5_out9),
    .out10(demultiplexer_5_out10), .out11(demultiplexer_5_out11), .out12(EXE_2), .in(S2), .sel(OP));  // open: out13, out14, out15
  Multiplexer #(.select(4), .width(16), .disabled(0), .enable("false")) multiplexer_2 (
    .in0({RF_VALA[15:12], RAMWADDR}), .in1({RF_VALA[15:12], RAMWADDR}), .in2({RF_VALA[15:12], RAMWADDR}),
    .in3({RF_VALA[15:12], RAMWADDR}), .in4(IMM), .in5({RF_VALA[15:12], RAMWADDR}),
    .in6({RF_VALA[15:12], RAMWADDR}), .in7({RF_VALA[15:12], RAMWADDR}), .in8({RF_VALA[15:12], RAMWADDR}),
    .in9({RF_VALA[15:12], RAMWADDR}), .in10({RF_VALA[15:12], RAMWADDR}), .in11({RF_VALA[15:12], RAMWADDR}),
    .in12({RF_VALA[15:12], RAMWADDR}), .in13({RF_VALA[15:12], RAMWADDR}), .in14({RF_VALA[15:12], RAMWADDR}),
    .in15({RF_VALA[15:12], RAMWADDR}), .out(ALUP1), .sel(OP));

  assign ALUOP = OP;
  assign ALUP2 = RAMWVAL;
  assign CMP_A = {RF_VALA[15:12], RAMWADDR};
  assign CMP_B = RAMWVAL;
  assign RF_CLK = EXE;
  assign RF_VALA[11:0] = RAMWADDR;
  assign RF_VALB = RAMWVAL;
  assign SETIPVAL = IMM[11:0];
endmodule

// CMP
module Comparison_Register (
  input  Compare,
  input  [15:0] A,
  input  [15:0] B,
  input  RST,
  output GT,
  output EQ,
  output LT,
  output LTE,
  output GTE
);

  wire [15:0] register_1_q, register_2_q;

  Register #(.width(16)) register_1 (.D(A), .Q(register_1_q), .clk(Compare), .clr(RST));  // open: en
  Register #(.width(16)) register_2 (.D(B), .Q(register_2_q), .clk(Compare), .clr(RST));  // open: en
  Comparator #(.width(16)) comparator_1 (.a(register_1_q), .b(register_2_q), .gt(GT), .eq(EQ), .lt(LT));
  or or_1 (LTE, LT, EQ);
  or or_2 (GTE, EQ, GT);
endmodule

// IPC
module IP_Controller (
  input  [2:0] OP,
  input  GT,
  input  EQ,
  input  LT,
  input  LTE,
  input  GTE,
  input  Clk,
  output SET
);

  wire multiplexer_1_out;

  Multiplexer #(.select(3), .enable("false")) multiplexer_1 (
    .in0(Clk), .in1(EQ), .in2(LT), .in3(GT), .in4(LTE), .in5(GTE), .in6(1'b0), .in7(1'b0),
    .out(multiplexer_1_out), .sel(OP));
  and and_1 (SET, multiplexer_1_out, Clk);
endmodule

module Register_Filer (
  input  [3:0] Dest,
  input  Clk,
  input  [15:0] Val,
  input  RST,
  input  [3:0] Src_A,
  input  [3:0] Src_B,
  output [15:0] Val_A,
  output [15:0] Val_B
);

  wire demultiplexer_1_out0, demultiplexer_1_out1, demultiplexer_1_out2, demultiplexer_1_out3,
       demultiplexer_1_out4, demultiplexer_1_out5, demultiplexer_1_out6, demultiplexer_1_out7,
       demultiplexer_1_out8, demultiplexer_1_out9, demultiplexer_1_out10, demultiplexer_1_out11,
       demultiplexer_1_out12, demultiplexer_1_out13, demultiplexer_1_out14, demultiplexer_1_out15;
  wire [15:0] register_1_q, register_2_q, register_3_q, register_4_q, register_5_q, register_6_q,
       register_7_q, register_8_q, register_9_q, register_10_q, register_11_q, register_12_q, register_13_q,
       register_14_q, register_15_q, register_16_q;

  Demultiplexer #(.select(4), .disabled(0), .enable("false")) demultiplexer_1 (
    .out0(demultiplexer_1_out0), .out1(demultiplexer_1_out1), .out2(demultiplexer_1_out2),
    .out3(demultiplexer_1_out3), .out4(demultiplexer_1_out4), .out5(demultiplexer_1_out5),
    .out6(demultiplexer_1_out6), .out7(demultiplexer_1_out7), .out8(demultiplexer_1_out8),
    .out9(demultiplexer_1_out9), .out10(demultiplexer_1_out10), .out11(demultiplexer_1_out11),
    .out12(demultiplexer_1_out12), .out13(demultiplexer_1_out13), .out14(demultiplexer_1_out14),
    .out15(demultiplexer_1_out15), .in(Clk), .sel(Dest));
  Register #(.width(16), .trigger("falling")) register_1 (
    .D(Val), .Q(register_1_q), .clk(demultiplexer_1_out0), .clr(RST));  // open: en
  Register #(.width(16), .trigger("falling")) register_2 (
    .D(Val), .Q(register_2_q), .clk(demultiplexer_1_out4), .clr(RST));  // open: en
  Register #(.width(16), .trigger("falling")) register_3 (
    .D(Val), .Q(register_3_q), .clk(demultiplexer_1_out8), .clr(RST));  // open: en
  Register #(.width(16), .trigger("falling")) register_4 (
    .D(Val), .Q(register_4_q), .clk(demultiplexer_1_out12), .clr(RST));  // open: en
  Register #(.width(16), .trigger("falling")) register_5 (
    .D(Val), .Q(register_5_q), .clk(demultiplexer_1_out1), .clr(RST));  // open: en
  Register #(.width(16), .trigger("falling")) register_6 (
    .D(Val), .Q(register_6_q), .clk(demultiplexer_1_out5), .clr(RST));  // open: en
  Register #(.width(16), .trigger("falling")) register_7 (
    .D(Val), .Q(register_7_q), .clk(demultiplexer_1_out9), .clr(RST));  // open: en
  Register #(.width(16), .trigger("falling")) register_8 (
    .D(Val), .Q(register_8_q), .clk(demultiplexer_1_out13), .clr(RST));  // open: en
  Register #(.width(16), .trigger("falling")) register_9 (
    .D(Val), .Q(register_9_q), .clk(demultiplexer_1_out2), .clr(RST));  // open: en
  Register #(.width(16), .trigger("falling")) register_10 (
    .D(Val), .Q(register_10_q), .clk(demultiplexer_1_out6), .clr(RST));  // open: en
  Register #(.width(16), .trigger("falling")) register_11 (
    .D(Val), .Q(register_11_q), .clk(demultiplexer_1_out10), .clr(RST));  // open: en
  Register #(.width(16), .trigger("falling")) register_12 (
    .D(Val), .Q(register_12_q), .clk(demultiplexer_1_out14), .clr(RST));  // open: en
  Register #(.width(16), .trigger("falling")) register_13 (
    .D(Val), .Q(register_13_q), .clk(demultiplexer_1_out3), .clr(RST));  // open: en
  Register #(.width(16), .trigger("falling")) register_14 (
    .D(Val), .Q(register_14_q), .clk(demultiplexer_1_out7), .clr(RST));  // open: en
  Register #(.width(16), .trigger("falling")) register_15 (
    .D(Val), .Q(register_15_q), .clk(demultiplexer_1_out11), .clr(RST));  // open: en
  Register #(.width(16), .trigger("falling")) register_16 (
    .D(Val), .Q(register_16_q), .clk(demultiplexer_1_out15), .clr(RST));  // open: en
  Multiplexer #(.select(4), .width(16), .disabled(0), .enable("false")) multiplexer_1 (
    .in0(register_1_q), .in1(register_5_q), .in2(register_9_q), .in3(register_13_q), .in4(register_2_q),
    .in5(register_6_q), .in6(register_10_q), .in7(register_14_q), .in8(register_3_q), .in9(register_7_q),
    .in10(register_11_q), .in11(register_15_q), .in12(register_4_q), .in13(register_8_q),
    .in14(register_12_q), .in15(register_16_q), .out(Val_A), .sel(Src_A));
  Multiplexer #(.select(4), .width(16), .disabled(0), .enable("false")) multiplexer_2 (
    .in0(register_1_q), .in1(register_5_q), .in2(register_9_q), .in3(register_13_q), .in4(register_2_q),
    .in5(register_6_q), .in6(register_10_q), .in7(register_14_q), .in8(register_3_q), .in9(register_7_q),
    .in10(register_11_q), .in11(register_15_q), .in12(register_4_q), .in13(register_8_q),
    .in14(register_12_q), .in15(register_16_q), .out(Val_B), .sel(Src_B));
endmodule

// ADDRBUS
module AddressBus (
  input  [11:0] Address,
  input  [15:0] WriteValue,
  input  RW,
  input  Clk,
  input  Exe,
  input  [15:0] RAM_Read_Value,
  input  S1,
  output [15:0] ReadValue,
  output [11:0] RAM_Address,
  output [15:0] RAM_Write_Value,
  output Prepare,
  output NEXT
);

  wire not_1_out;
  wire [15:0] bidirectional_or_3_out, controlled_buffer_1_out, controlled_buffer_2_out;

  Register #(.width(1)) register_1 (.D(RW), .Q(Prepare), .clk(RW), .clr(S1));  // open: en
  Bidirectional_OR bidirectional_or_1 (.In(bidirectional_or_3_out), .Out(ReadValue), .Enable(Exe));
  and and_1 (NEXT, Clk, Exe, Prepare);
  Register #(.width(12)) register_2 (.D(Address), .Q(RAM_Address), .clk(Clk), .clr(S1));  // open: en
  assign controlled_buffer_1_out = Prepare ? WriteValue : 16'bz;  // Controlled_Buffer controlled_buffer_1
  not not_1 (not_1_out, Prepare);
  Bidirectional_OR bidirectional_or_2 (.In(controlled_buffer_1_out), .Out(RAM_Write_Value), .Enable(Prepare));
  Bidirectional_OR bidirectional_or_3 (.In(controlled_buffer_2_out), .Out(bidirectional_or_3_out), .Enable(not_1_out));
  assign controlled_buffer_2_out = Exe ? RAM_Read_Value : 16'bz;  // Controlled_Buffer controlled_buffer_2
endmodule

module Bidirectional_OR (
  input  Enable,
  input  [15:0] In,
  output [15:0] Out
);

  wire [15:0] multiplexer_1_out;

  Multiplexer #(.width(16), .disabled(0), .enable("false")) multiplexer_1 (
    .in0({16{1'b0}}), .in1(In), .out(multiplexer_1_out), .sel(Enable));
  assign Out = {16{1'b0}} | multiplexer_1_out;  // OR_Gate or_1, 16 bits wide
endmodule

module Test (
  input  Direction,
  input  [15:0] B_In,
  input  [15:0] A_In,
  output [15:0] A_Out,
  output [15:0] B_Out
);

  wire not_1_out;

  assign A_Out = not_1_out ? B_In : 16'bz;  // Controlled_Buffer controlled_buffer_1
  not not_1 (not_1_out, Direction);
  assign B_Out = Direction ? A_In : 16'bz;  // Controlled_Buffer controlled_buffer_2
endmodule

// PC Controller
module PC_Controller_2_0 (
  input  [15:0] Reg_Value_A,
  input  [15:0] Reg_Value_B,
  input  [15:0] ALU_Result,
  input  [15:0] RAM_Read_Value,
  input  [3:0] OP,
  input  [3:0] OPER1,
  input  [3:0] OPER2,
  input  [3:0] OPER3,
  input  [15:0] IMM,
  input  S2,
  input  S3,
  output Write,
  output [3:0] Reg_Destination,
  output [3:0] Reg_Src_A,
  output [3:0] Reg_Src_B,
  output [15:0] Reg_Destination_Value,
  output [3:0] ALU_Operation,
  output [15:0] ALU_Param_1,
  output [15:0] ALU_Parameter_2,
  output ALU_Exe,
  output [15:0] Compare_A,
  output [11:0] RAM_Address,
  output [15:0] Compare_B,
  output [15:0] RAM_Write_Value,
  output Compare,
  output [2:0] PC_Op,
  output Read_Write,
  output PC_Exe,
  output RAM_Clk,
  output [11:0] IP_Set_To,
  output RAM_Exe,
  output Next_Opcode,
  output Get_Next_Value
);

  wire demultiplexer_5_out0, demultiplexer_5_out1, demultiplexer_5_out2, demultiplexer_5_out3,
       demultiplexer_5_out6, demultiplexer_5_out7, demultiplexer_5_out8, demultiplexer_5_out9,
       demultiplexer_5_out10, demultiplexer_5_out11, demultiplexer_5_out12, demultiplexer_6_out0,
       demultiplexer_6_out1, demultiplexer_6_out2, demultiplexer_6_out3, demultiplexer_6_out4,
       demultiplexer_6_out5, demultiplexer_6_out6, demultiplexer_6_out7, demultiplexer_6_out8,
       demultiplexer_6_out9, demultiplexer_6_out10, demultiplexer_6_out11, demultiplexer_6_out12,
       demultiplexer_6_out13, demultiplexer_6_out14, demultiplexer_6_out15;
  wire [3:0] demultiplexer_1_out0, demultiplexer_1_out1, demultiplexer_1_out2, demultiplexer_1_out3,
       demultiplexer_1_out4, demultiplexer_1_out5, demultiplexer_1_out12, demultiplexer_1_out13,
       demultiplexer_2_out0, demultiplexer_2_out1, demultiplexer_2_out2, demultiplexer_2_out3,
       demultiplexer_2_out4, demultiplexer_2_out5, demultiplexer_2_out12, demultiplexer_2_out13,
       demultiplexer_3_out0, demultiplexer_3_out1, demultiplexer_3_out2, demultiplexer_3_out3,
       demultiplexer_3_out4;
  wire [15:0] demultiplexer_4_out4, demultiplexer_4_out6, demultiplexer_4_out7, demultiplexer_4_out8,
       demultiplexer_4_out9, demultiplexer_4_out10, demultiplexer_4_out11;
  wire [15:12] or_4_out;

  or or_1 (Write, demultiplexer_6_out4, ALU_Exe, demultiplexer_5_out12);
  assign Reg_Destination = demultiplexer_1_out0 | demultiplexer_1_out1 | demultiplexer_1_out2 | demultiplexer_1_out3 | demultiplexer_1_out4 | demultiplexer_1_out12;  // OR_Gate or_2, 4 bits wide
  Subtractor #(.width(3)) subtractor_1 (.a(OP[2:0]), .b(3'b110), .out(PC_Op));  // open: bin, bout
  or or_3 (PC_Exe, demultiplexer_5_out6, demultiplexer_5_out7, demultiplexer_5_out8, demultiplexer_5_out9, demultiplexer_5_out10, demultiplexer_5_out11);
  assign {or_4_out, IP_Set_To} = demultiplexer_4_out10 | demultiplexer_4_out9 | demultiplexer_4_out8 | demultiplexer_4_out7 | demultiplexer_4_out6 | demultiplexer_4_out11;  // OR_Gate or_4, 16 bits wide
  or or_5 (Next_Opcode, demultiplexer_6_out15, demultiplexer_6_out14, demultiplexer_6_out12, demultiplexer_6_out11, demultiplexer_6_out10, demultiplexer_6_out9, demultiplexer_6_out8, demultiplexer_6_out7, demultiplexer_6_out6, demultiplexer_6_out5, demultiplexer_6_out3, demultiplexer_6_out2, demultiplexer_6_out1, demultiplexer_6_out0);
  Demultiplexer #(.select(4), .width(4), .disabled(0), .enable("false")) demultiplexer_1 (
    .out0(demultiplexer_1_out0), .out1(demultiplexer_1_out1), .out2(demultiplexer_1_out2),
    .out3(demultiplexer_1_out3), .out4(demultiplexer_1_out4), .out5(demultiplexer_1_out5),
    .out12(demultiplexer_1_out12), .out13(demultiplexer_1_out13), .in(OPER1), .sel(OP));  // open: out6, out7, out8, out9, out10, out11, out14, out15
  assign Reg_Destination_Value = RAM_Read_Value | demultiplexer_4_out4 | ALU_Result;  // OR_Gate or_6, 16 bits wide
  assign Reg_Src_A = demultiplexer_2_out0 | demultiplexer_2_out1 | demultiplexer_2_out2 | demultiplexer_2_out3 | demultiplexer_2_out4 | demultiplexer_2_out12 | demultiplexer_1_out13 | demultiplexer_1_out5;  // OR_Gate or_7, 4 bits wide
  Demultiplexer #(.select(4), .width(4), .disabled(0), .enable("false")) demultiplexer_2 (
    .out0(demultiplexer_2_out0), .out1(demultiplexer_2_out1), .out2(demultiplexer_2_out2),
    .out3(demultiplexer_2_out3), .out4(demultiplexer_2_out4), .out5(demultiplexer_2_out5),
    .out12(demultiplexer_2_out12), .out13(demultiplexer_2_out13), .in(OPER2), .sel(OP));  // open: out6, out7, out8, out9, out10, out11, out14, out15
  assign Reg_Src_B = demultiplexer_2_out13 | demultiplexer_3_out0 | demultiplexer_3_out1 | demultiplexer_3_out2 | demultiplexer_3_out3 | demultiplexer_3_out4 | demultiplexer_2_out5;  // OR_Gate or_8, 4 bits wide
  Demultiplexer #(.select(4), .width(4), .disabled(0), .enable("false")) demultiplexer_3 (
    .out0(demultiplexer_3_out0), .out1(demultiplexer_3_out1), .out2(demultiplexer_3_out2),
    .out3(demultiplexer_3_out3), .out4(demultiplexer_3_out4), .in(OPER3), .sel(OP));  // open: out5, out6, out7, out8, out9, out10, out11, out12, out13, out14, out15
  Demultiplexer #(.select(4), .width(16), .disabled(0), .enable("false")) demultiplexer_4 (
    .out4(demultiplexer_4_out4), .out6(demultiplexer_4_out6), .out7(demultiplexer_4_out7),
    .out8(demultiplexer_4_out8), .out9(demultiplexer_4_out9), .out10(demultiplexer_4_out10),
    .out11(demultiplexer_4_out11), .in(IMM), .sel(OP));  // open: out0, out1, out2, out3, out5, out12, out13, out14, out15
  or or_9 (ALU_Exe, demultiplexer_5_out0, demultiplexer_5_out1, demultiplexer_5_out2, demultiplexer_5_out3);
  Demultiplexer #(.select(4), .disabled(0), .enable("false")) demultiplexer_5 (
    .out0(demultiplexer_5_out0), .out1(demultiplexer_5_out1), .out2(demultiplexer_5_out2),
    .out3(demultiplexer_5_out3), .out4(Get_Next_Value), .out5(Compare), .out6(demultiplexer_5_out6),
    .out7(demultiplexer_5_out7), .out8(demultiplexer_5_out8), .out9(demultiplexer_5_out9),
    .out10(demultiplexer_5_out10), .out11(demultiplexer_5_out11), .out12(demultiplexer_5_out12),
    .out13(Read_Write), .in(S2), .sel(OP));  // open: out14, out15
  Demultiplexer #(.select(4), .disabled(0), .enable("false")) demultiplexer_6 (
    .out0(demultiplexer_6_out0), .out1(demultiplexer_6_out1), .out2(demultiplexer_6_out2),
    .out3(demultiplexer_6_out3), .out4(demultiplexer_6_out4), .out5(demultiplexer_6_out5),
    .out6(demultiplexer_6_out6), .out7(demultiplexer_6_out7), .out8(demultiplexer_6_out8),
    .out9(demultiplexer_6_out9), .out10(demultiplexer_6_out10), .out11(demultiplexer_6_out11),
    .out12(demultiplexer_6_out12), .out13(demultiplexer_6_out13), .out14(demultiplexer_6_out14),
    .out15(demultiplexer_6_out15), .in(S3), .sel(OP));
  or or_10 (RAM_Clk, Read_Write, demultiplexer_6_out13, demultiplexer_5_out12);
  or or_11 (RAM_Exe, demultiplexer_5_out12, demultiplexer_6_out13);

  assign ALU_Operation = OP;
  assign ALU_Param_1 = Reg_Value_A;
  assign ALU_Parameter_2 = Reg_Value_B;
  assign Compare_A = Reg_Value_A;
  assign Compare_B = Reg_Value_B;
  assign RAM_Address = Reg_Value_A[11:0];
  assign RAM_Write_Value = Reg_Value_B;
endmodule
